// Logisim project Shmerlard8.circ as structural Verilog: 5 circuits, main circuit main
module main (
  input  [7:0] in_1,
  input  MAN,
  input  MAR_WR_EN,
  input  MDR_WR_EN,
  input  RST,
  input  r_W,
  input  MDR_OUT_EN,
  input  b_M
);

  wire CLK, memory_registers_1_ram_wr_en;
  wire [7:0] controlled_buffer_1_out, HL_q, memory_registers_1_mem_data_out, ram_1_dout;
  wire [15:0] memory_registers_1_mem_address_out;

  Clock clock_1 (.out(CLK));
  assign controlled_buffer_1_out = MAN ? in_1 : 8'bz;  // Controlled_Buffer controlled_buffer_1
  // Probe on controlled_buffer_1_out
  Register HL (.en(1'b0), .clk(CLK), .Q(HL_q));  // open: D, clr
  memory_registers memory_registers_1 (
    .REG_L(HL_q), .MAR_WR_EN(MAR_WR_EN), .REG_H(HL_q), .DATA_IN(controlled_buffer_1_out),
    .MDR_WR_EN(MDR_WR_EN), .b_M(b_M), .r_W(r_W), .MDR_OUT_EN(MDR_OUT_EN), .CLK(CLK),
    .MEM_DATA_IN(ram_1_dout), .MEM_ADDRESS_OUT(memory_registers_1_mem_address_out),
    .DATA_OUT(controlled_buffer_1_out), .MEM_DATA_OUT(memory_registers_1_mem_data_out),
    .RAM_WR_EN(memory_registers_1_ram_wr_en));  // open: RST
  // Probe on memory_registers_1_mem_address_out
  RAM #(.addrWidth(16)) ram_1 (
    .addr(memory_registers_1_mem_address_out), .we(memory_registers_1_ram_wr_en), .oe(1'b1), .clk(CLK),
    .din(memory_registers_1_mem_data_out), .dout(ram_1_dout));
  // Probe on ram_1_dout
endmodule

module register_file (
  input  CLK,
  input  RST,
  input  [7:0] DATA_IN,
  input  [2:0] REG_SEL,
  input  REG_WR,
  input  REG_RD,
  output [7:0] DATA_OUT
);

  wire RD_A, RD_B, RD_C, RD_D, RD_F, RD_H, RD_L, RD_SP, WE_A, WE_B, WE_C, WE_D, WE_F, WE_H, WE_L, WE_SP;
  wire [7:0] A_REG_q, B_REG_q, C_REG_q, D_REG_q, F_REG_q, H_REG_q, L_REG_q, SP_REG_q;

  Decoder #(.select(3)) decoder_1 (
    .out0(WE_SP), .out1(WE_A), .out2(WE_B), .out3(WE_C), .out4(WE_D), .out5(WE_L), .out6(WE_H), .out7(WE_F),
    .sel(REG_SEL), .en(REG_WR));
  Decoder #(.select(3)) decoder_2 (
    .out0(RD_SP), .out1(RD_A), .out2(RD_B), .out3(RD_C), .out4(RD_D), .out5(RD_L), .out6(RD_H), .out7(RD_F),
    .sel(REG_SEL), .en(REG_RD));
  Register SP_REG (.D(DATA_IN), .en(WE_SP), .clk(CLK), .Q(SP_REG_q), .clr(RST));
  Register A_REG (.D(DATA_IN), .en(WE_A), .clk(CLK), .Q(A_REG_q), .clr(RST));
  Register B_REG (.D(DATA_IN), .en(WE_B), .clk(CLK), .Q(B_REG_q), .clr(RST));
  Register C_REG (.D(DATA_IN), .en(WE_C), .clk(CLK), .Q(C_REG_q), .clr(RST));
  Register D_REG (.D(DATA_IN), .en(WE_D), .clk(CLK), .Q(D_REG_q), .clr(RST));
  Register L_REG (.D(DATA_IN), .en(WE_L), .clk(CLK), .Q(L_REG_q), .clr(RST));
  Register H_REG (.D(DATA_IN), .en(WE_H), .clk(CLK), .Q(H_REG_q), .clr(RST));
  Register F_REG (.D(DATA_IN), .en(WE_F), .clk(CLK), .Q(F_REG_q), .clr(RST));
  assign DATA_OUT = RD_SP ? SP_REG_q : 8'bz;  // Controlled_Buffer controlled_buffer_1
  assign DATA_OUT = RD_A ? A_REG_q : 8'bz;  // Controlled_Buffer controlled_buffer_2
  assign DATA_OUT = RD_B ? B_REG_q : 8'bz;  // Controlled_Buffer controlled_buffer_3
  assign DATA_OUT = RD_C ? C_REG_q : 8'bz;  // Controlled_Buffer controlled_buffer_4
  assign DATA_OUT = RD_D ? D_REG_q : 8'bz;  // Controlled_Buffer controlled_buffer_5
  assign DATA_OUT = RD_L ? L_REG_q : 8'bz;  // Controlled_Buffer controlled_buffer_6
  assign DATA_OUT = RD_H ? H_REG_q : 8'bz;  // Controlled_Buffer controlled_buffer_7
  assign DATA_OUT = RD_F ? F_REG_q : 8'bz;  // Controlled_Buffer controlled_buffer_8
endmodule

module instruction_register (
  input  CLK,
  input  IR_OUT,
  input  [7:0] MDR_IN,
  input  IR_SEL,
  input  IR_IN,
  input  RF_SEL,
  output [7:0] DATA_OUT,
  output [4:0] OP_CODE5,
  output [2:0] REG_SEL
);

  wire decoder_1_out0, decoder_1_out1;
  wire [2:0] REG_SEL_H, REG_SEL_L;
  wire [7:3] IR_L_q;

  Decoder decoder_1 (.out0(decoder_1_out0), .out1(decoder_1_out1), .sel(IR_SEL), .en(IR_IN));
  Multiplexer #(.width(3)) multiplexer_1 (.in0(REG_SEL_L), .in1(REG_SEL_H), .out(REG_SEL), .sel(RF_SEL));
  Register IR_L (.D(MDR_IN), .en(decoder_1_out0), .clk(CLK), .Q({IR_L_q, REG_SEL_L}));  // open: clr
  Register IR_H (.D(MDR_IN), .en(decoder_1_out1), .clk(CLK), .Q({OP_CODE5, REG_SEL_H}));  // open: clr
  assign DATA_OUT = IR_OUT ? {IR_L_q, REG_SEL_L} : 8'bz;  // Controlled_Buffer controlled_buffer_1

  // Other names for the same wires on the sheet: OP_CODE[4:0] = OP_CODE5; IR_L_O = IR_OUT
endmodule

module timing_control (
  input  TC_RST,
  input  CLK,
  output [4:0] T_OUT
);

  Counter #(.max('h1f), .width(5)) counter_1 (
    .clr(TC_RST), .load(1'b0), .up(1'b1), .count(1'b1), .clk(CLK), .Q(T_OUT));  // open: D, carry
endmodule

module memory_registers (
  input  CLK,
  input  RST,
  input  [7:0] REG_L,
  input  MAR_WR_EN,
  input  [7:0] REG_H,
  input  [7:0] MEM_DATA_IN,
  input  [7:0] DATA_IN,
  input  MDR_WR_EN,
  input  b_M,
  input  r_W,
  input  MDR_OUT_EN,
  output [15:0] MEM_ADDRESS_OUT,
  output [7:0] DATA_OUT,
  output [7:0] MEM_DATA_OUT,
  output RAM_WR_EN
);

  wire and_1_out, and_2_out, and_3_out, not_1_out, not_2_out;
  wire [7:0] controlled_buffer_1_out, MDR_q;

  assign controlled_buffer_1_out = not_1_out ? DATA_IN : 8'bz;  // Controlled_Buffer controlled_buffer_1
  not not_1 (not_1_out, b_M);
  assign controlled_buffer_1_out = and_1_out ? MEM_DATA_IN : 8'bz;  // Controlled_Buffer controlled_buffer_2
  Register MAR_L (.D(REG_L), .en(MAR_WR_EN), .clk(CLK), .Q(MEM_ADDRESS_OUT[7:0]), .clr(RST));
  Register MAR_H (.D(REG_H), .en(MAR_WR_EN), .clk(CLK), .Q(MEM_ADDRESS_OUT[15:8]), .clr(RST));
  Register MDR (.D(controlled_buffer_1_out), .en(MDR_WR_EN), .clk(CLK), .Q(MDR_q), .clr(RST));
  not not_2 (not_2_out, r_W);
  and and_1 (and_1_out, b_M, not_2_out);
  assign MEM_DATA_OUT = and_2_out ? MDR_q : 8'bz;  // Controlled_Buffer controlled_buffer_3
  and and_2 (and_2_out, r_W, MDR_OUT_EN);
  and and_3 (and_3_out, not_1_out, MDR_OUT_EN);
  assign DATA_OUT = and_3_out ? MDR_q : 8'bz;  // Controlled_Buffer controlled_buffer_4

  assign RAM_WR_EN = r_W;
endmodule
